// Logisim project 4 Prova.circ as structural Verilog: 1 circuit, main circuit main
module main (
  input  t,
  input  h,
  input  r,
  input  c,
  output x
);

  wire and_1_out, not_1_out, not_2_out;

  not not_1 (not_1_out, c);
  and and_1 (and_1_out, t, not_2_out);
  not not_2 (not_2_out, h);
  or or_1 (x, not_1_out, and_1_out);
endmodule
