// Logisim project 2d.circ as structural Verilog
module _2x (
  input  a,
  input  b,
  input  c,
  output x
);

  wire and_1_out, not_1_out, not_2_out, not_3_out, or_1_out, or_2_out, or_3_out;

  not not_1 (not_1_out, b);
  or or_1 (or_1_out, a, c);
  not not_2 (not_2_out, c);
  and and_1 (and_1_out, a, not_1_out, or_1_out);
  or or_2 (or_2_out, a, not_2_out);
  or or_3 (or_3_out, b, and_1_out);
  not not_3 (not_3_out, b);
  and and_2 (x, or_2_out, or_3_out, not_3_out);
endmodule
