// Logisim project 2f.circ as structural Verilog: 1 circuit, main circuit main
module main (
  input  in_1,
  input  in_2,
  input  in_3,
  output out_4
);

  wire and_1_out, not_1_out, not_2_out, or_1_out, xnor_1_out;

  xnor xnor_1 (xnor_1_out, in_1, in_2);
  not not_1 (not_1_out, not_2_out);
  not not_2 (not_2_out, in_3);
  or or_1 (or_1_out, xnor_1_out, in_2);
  and and_1 (and_1_out, in_1, in_2, in_3, not_1_out);
  and and_2 (out_4, or_1_out, and_1_out);
endmodule
