// Logisim project XOR Differences.circ as structural Verilog: 1 circuit, main circuit main
module main (
  input  in_1,
  input  in_2,
  input  in_3,
  input  in_4,
  input  in_5,
  input  in_6,
  output out_7,
  output out_8
);

  wire xor_2_out;

  ExactlyOne xor_1 (.out(out_7), .in0(in_1), .in2(in_2), .in4(in_3));
  xor xor_2 (xor_2_out, in_4, in_5);
  xor xor_3 (out_8, xor_2_out, in_6);
endmodule
