// Logisim project Calculadora - Matheus Henrique Schaly.circ as structural Verilog: 12 circuits, main circuit MSomador
module main (
  input  [15:0] in_1,
  input  [15:0] in_2,
  output [15:0] out_3
);

  wire and_2_out, and_3_out, and_4_out, and_out, \botões_1_out_5 , \botões_1_out_6 , button_2_out,
       button_3_out, button_4_out, button_out, not_1_out, not_2_out, not_3_out, not_4_out;
  wire [15:0] controlled_buffer_1_out, controlled_buffer_2_out, controlled_buffer_3_out,
       controlled_buffer_4_out, controlled_buffer_5_out, controlled_buffer_6_out, controlled_buffer_7_out,
       controlled_buffer_8_out, divisor_out_3, multiplicador_1_out_3, somador_16_bits_out_3,
       subtrator_16_bits_out_3;

  Button button (.out(button_out));
  Button button_2 (.out(button_2_out));
  Button button_3 (.out(button_3_out));
  Button button_4 (.out(button_4_out));
  \Botões  \botões_1  (
    .b1(button_out), .b2(button_2_out), .out_5(\botões_1_out_5 ), .b3(button_3_out),
    .out_6(\botões_1_out_6 ), .b4(button_4_out));
  not not_1 (not_1_out, \botões_1_out_5 );
  not not_2 (not_2_out, \botões_1_out_6 );
  and \and  (and_out, not_1_out, not_2_out);
  not not_3 (not_3_out, \botões_1_out_6 );
  not not_4 (not_4_out, \botões_1_out_5 );
  and and_2 (and_2_out, not_3_out, \botões_1_out_5 );
  and and_3 (and_3_out, \botões_1_out_6 , \botões_1_out_5 );
  and and_4 (and_4_out, not_4_out, \botões_1_out_6 );
  assign controlled_buffer_1_out = and_out ? in_1 : 16'bz;  // Controlled_Buffer controlled_buffer_1
  Somador_16_Bits somador_16_bits (
    .in_1(controlled_buffer_1_out), .in_2(controlled_buffer_2_out), .out_3(somador_16_bits_out_3));
  assign controlled_buffer_2_out = and_out ? in_2 : 16'bz;  // Controlled_Buffer controlled_buffer_2
  assign controlled_buffer_3_out = and_2_out ? in_1 : 16'bz;  // Controlled_Buffer controlled_buffer_3
  assign controlled_buffer_4_out = and_2_out ? in_2 : 16'bz;  // Controlled_Buffer controlled_buffer_4
  assign controlled_buffer_5_out = and_4_out ? in_1 : 16'bz;  // Controlled_Buffer controlled_buffer_5
  Subtrator_16_Bits subtrator_16_bits (
    .in_1(controlled_buffer_5_out), .in_2(controlled_buffer_6_out), .out_3(subtrator_16_bits_out_3));
  assign controlled_buffer_6_out = and_4_out ? in_2 : 16'bz;  // Controlled_Buffer controlled_buffer_6
  assign controlled_buffer_7_out = and_3_out ? in_1 : 16'bz;  // Controlled_Buffer controlled_buffer_7
  assign controlled_buffer_8_out = and_3_out ? in_2 : 16'bz;  // Controlled_Buffer controlled_buffer_8
  assign out_3 = and_out ? somador_16_bits_out_3 : 16'bz;  // Controlled_Buffer controlled_buffer_9
  Multiplicador multiplicador_1 (
    .in_1(controlled_buffer_3_out), .in_2(controlled_buffer_4_out), .out_3(multiplicador_1_out_3));
  assign out_3 = and_2_out ? multiplicador_1_out_3 : 16'bz;  // Controlled_Buffer controlled_buffer_10
  assign out_3 = and_4_out ? subtrator_16_bits_out_3 : 16'bz;  // Controlled_Buffer controlled_buffer_11
  Divisor divisor (.in_1(controlled_buffer_7_out), .in_2(controlled_buffer_8_out), .out_3(divisor_out_3));
  assign out_3 = and_3_out ? divisor_out_3 : 16'bz;  // Controlled_Buffer controlled_buffer_12
endmodule

module Multiplicador_2_Bits (
  input  in_1,
  input  in_2,
  input  in_3,
  input  in_4,
  output out_5,
  output out_6,
  output out_7,
  output out_8
);

  wire and_1_out, and_3_out, and_4_out, and_5_out;

  and and_1 (and_1_out, in_1, in_4);
  and and_2 (out_5, in_1, in_3);
  and and_3 (and_3_out, in_2, in_3);
  and and_4 (and_4_out, in_2, in_4);
  xor xor_1 (out_6, and_1_out, and_3_out);
  and and_5 (and_5_out, and_1_out, and_3_out);
  xor xor_2 (out_7, and_5_out, and_4_out);
  and and_6 (out_8, and_5_out, and_4_out);
endmodule

module MSomador (
  input  A,
  input  B,
  output out_3,
  output out_4
);

  and and_1 (out_3, A, B);
  xor xor_1 (out_4, A, B);
endmodule

module MSubtrator (
  input  A,
  input  B,
  output out_3,
  output out_4
);

  wire not_1_out;

  not not_1 (not_1_out, A);
  and and_1 (out_4, B, not_1_out);
  xor xor_1 (out_3, A, B);
endmodule

module SomadorC (
  input  A,
  input  B,
  input  C,
  output out_4,
  output out_5
);

  wire and_1_out, and_2_out, xor_1_out, xor_2_out;

  xor xor_1 (xor_1_out, A, B);
  xor xor_2 (xor_2_out, B, C);
  xor xor_3 (out_4, xor_1_out, C);
  and and_1 (and_1_out, C, B);
  and and_2 (and_2_out, A, xor_2_out);
  or or_1 (out_5, and_1_out, and_2_out);
endmodule

module SubtratorC (
  input  A,
  input  B,
  input  C,
  output out_4,
  output out_5
);

  wire and_1_out, and_2_out, not_1_out, not_2_out, xor_1_out;

  not not_1 (not_1_out, xor_1_out);
  xor xor_1 (xor_1_out, A, B);
  and and_1 (and_1_out, not_1_out, C);
  not not_2 (not_2_out, A);
  xor xor_2 (out_4, xor_1_out, C);
  and and_2 (and_2_out, not_2_out, B);
  or or_1 (out_5, and_1_out, and_2_out);
endmodule

module Somador_16_Bits (
  input  [15:0] in_1,
  input  [15:0] in_2,
  output [15:0] out_3
);

  wire msomador_1_out_4, somadorc_2_out_5, somadorc_3_out_5, somadorc_4_out_5, somadorc_5_out_5,
       somadorc_6_out_5, somadorc_7_out_5, somadorc_8_out_5, somadorc_9_out_5, somadorc_10_out_5,
       somadorc_11_out_5, somadorc_12_out_5, somadorc_13_out_5, somadorc_14_out_5, somadorc_15_out_5;

  SomadorC somadorc_1 (.A(somadorc_2_out_5), .B(in_1[15]), .C(in_2[15]), .out_4(out_3[15]));  // open: out_5
  SomadorC somadorc_2 (.A(somadorc_3_out_5), .B(in_1[14]), .C(in_2[14]), .out_4(out_3[14]), .out_5(somadorc_2_out_5));
  SomadorC somadorc_3 (.A(somadorc_4_out_5), .B(in_1[13]), .C(in_2[13]), .out_4(out_3[13]), .out_5(somadorc_3_out_5));
  SomadorC somadorc_4 (.A(somadorc_6_out_5), .B(in_1[12]), .C(in_2[12]), .out_4(out_3[12]), .out_5(somadorc_4_out_5));
  SomadorC somadorc_5 (.A(somadorc_7_out_5), .B(in_1[10]), .C(in_2[10]), .out_4(out_3[10]), .out_5(somadorc_5_out_5));
  SomadorC somadorc_6 (.A(somadorc_5_out_5), .B(in_1[11]), .C(in_2[11]), .out_4(out_3[11]), .out_5(somadorc_6_out_5));
  SomadorC somadorc_7 (.A(somadorc_8_out_5), .B(in_1[9]), .C(in_2[9]), .out_4(out_3[9]), .out_5(somadorc_7_out_5));
  SomadorC somadorc_8 (.A(somadorc_10_out_5), .B(in_1[8]), .C(in_2[8]), .out_4(out_3[8]), .out_5(somadorc_8_out_5));
  SomadorC somadorc_9 (.A(somadorc_12_out_5), .B(in_1[6]), .C(in_2[6]), .out_4(out_3[6]), .out_5(somadorc_9_out_5));
  SomadorC somadorc_10 (.A(somadorc_9_out_5), .B(in_1[7]), .C(in_2[7]), .out_4(out_3[7]), .out_5(somadorc_10_out_5));
  SomadorC somadorc_11 (.A(somadorc_13_out_5), .B(in_1[4]), .C(in_2[4]), .out_4(out_3[4]), .out_5(somadorc_11_out_5));
  SomadorC somadorc_12 (.A(somadorc_11_out_5), .B(in_1[5]), .C(in_2[5]), .out_4(out_3[5]), .out_5(somadorc_12_out_5));
  SomadorC somadorc_13 (.A(somadorc_14_out_5), .B(in_1[3]), .C(in_2[3]), .out_4(out_3[3]), .out_5(somadorc_13_out_5));
  SomadorC somadorc_14 (.A(somadorc_15_out_5), .B(in_1[2]), .C(in_2[2]), .out_4(out_3[2]), .out_5(somadorc_14_out_5));
  SomadorC somadorc_15 (.A(msomador_1_out_4), .B(in_1[1]), .C(in_2[1]), .out_4(out_3[1]), .out_5(somadorc_15_out_5));
  MSomador msomador_1 (.A(in_1[0]), .B(in_2[0]), .out_3(out_3[0]), .out_4(msomador_1_out_4));
endmodule

module Subtrator_16_Bits (
  input  [15:0] in_1,
  input  [15:0] in_2,
  output [15:0] out_3
);

  wire msubtrator_1_out_3, subtratorc_1_out_5, subtratorc_3_out_5, subtratorc_4_out_5, subtratorc_5_out_5,
       subtratorc_6_out_5, subtratorc_7_out_5, subtratorc_8_out_5, subtratorc_9_out_5, subtratorc_10_out_5,
       subtratorc_11_out_5, subtratorc_12_out_5, subtratorc_13_out_5, subtratorc_14_out_5,
       subtratorc_15_out_5;

  SubtratorC subtratorc_1 (
    .A(subtratorc_4_out_5), .B(in_1[14]), .C(in_2[14]), .out_4(out_3[14]), .out_5(subtratorc_1_out_5));
  SubtratorC subtratorc_2 (.A(subtratorc_1_out_5), .B(in_1[15]), .C(in_2[15]), .out_4(out_3[15]));  // open: out_5
  SubtratorC subtratorc_3 (
    .A(subtratorc_6_out_5), .B(in_1[12]), .C(in_2[12]), .out_4(out_3[12]), .out_5(subtratorc_3_out_5));
  SubtratorC subtratorc_4 (
    .A(subtratorc_3_out_5), .B(in_1[13]), .C(in_2[13]), .out_4(out_3[13]), .out_5(subtratorc_4_out_5));
  SubtratorC subtratorc_5 (
    .A(subtratorc_8_out_5), .B(in_1[10]), .C(in_2[10]), .out_4(out_3[10]), .out_5(subtratorc_5_out_5));
  SubtratorC subtratorc_6 (
    .A(subtratorc_5_out_5), .B(in_1[11]), .C(in_2[11]), .out_4(out_3[11]), .out_5(subtratorc_6_out_5));
  SubtratorC subtratorc_7 (
    .A(subtratorc_10_out_5), .B(in_1[8]), .C(in_2[8]), .out_4(out_3[8]), .out_5(subtratorc_7_out_5));
  SubtratorC subtratorc_8 (
    .A(subtratorc_7_out_5), .B(in_1[9]), .C(in_2[9]), .out_4(out_3[9]), .out_5(subtratorc_8_out_5));
  SubtratorC subtratorc_9 (
    .A(subtratorc_11_out_5), .B(in_1[6]), .C(in_2[6]), .out_4(out_3[6]), .out_5(subtratorc_9_out_5));
  SubtratorC subtratorc_10 (
    .A(subtratorc_9_out_5), .B(in_1[7]), .C(in_2[7]), .out_4(out_3[7]), .out_5(subtratorc_10_out_5));
  SubtratorC subtratorc_11 (
    .A(subtratorc_12_out_5), .B(in_1[5]), .C(in_2[5]), .out_4(out_3[5]), .out_5(subtratorc_11_out_5));
  SubtratorC subtratorc_12 (
    .A(subtratorc_13_out_5), .B(in_1[4]), .C(in_2[4]), .out_4(out_3[4]), .out_5(subtratorc_12_out_5));
  SubtratorC subtratorc_13 (
    .A(subtratorc_14_out_5), .B(in_1[3]), .C(in_2[3]), .out_4(out_3[3]), .out_5(subtratorc_13_out_5));
  SubtratorC subtratorc_14 (
    .A(subtratorc_15_out_5), .B(in_1[2]), .C(in_2[2]), .out_4(out_3[2]), .out_5(subtratorc_14_out_5));
  SubtratorC subtratorc_15 (
    .A(msubtrator_1_out_3), .B(in_1[1]), .C(in_2[1]), .out_4(out_3[1]), .out_5(subtratorc_15_out_5));
  MSubtrator msubtrator_1 (.A(in_1[0]), .B(in_2[0]), .out_4(out_3[0]), .out_3(msubtrator_1_out_3));
endmodule

module Inversor (
  input  [15:0] in_1,
  output [15:0] out_2
);

  not not_1 (out_2[0], in_1[0]);
  not not_2 (out_2[1], in_1[1]);
  not not_3 (out_2[2], in_1[2]);
  not not_4 (out_2[3], in_1[3]);
  not not_5 (out_2[4], in_1[4]);
  not not_6 (out_2[5], in_1[5]);
  not not_7 (out_2[6], in_1[6]);
  not not_8 (out_2[7], in_1[7]);
  not not_9 (out_2[8], in_1[8]);
  not not_10 (out_2[9], in_1[9]);
  not not_11 (out_2[10], in_1[10]);
  not not_12 (out_2[11], in_1[11]);
  not not_13 (out_2[12], in_1[12]);
  not not_14 (out_2[13], in_1[13]);
  not not_15 (out_2[14], in_1[14]);
  not not_16 (out_2[15], in_1[15]);
endmodule

module \Botões  (
  input  b1,
  input  b2,
  input  b3,
  input  b4,
  output out_5,
  output out_6
);

  wire and_1_out, and_2_out, not_1_out, not_2_out;

  not not_1 (not_1_out, b1);
  not not_2 (not_2_out, b4);
  and and_1 (and_1_out, not_1_out, b3);
  and and_2 (and_2_out, b2, not_2_out);
  or or_1 (out_5, and_1_out, b4);
  or or_2 (out_6, and_2_out, b4);
endmodule

// *
module Multiplicador (
  input  [15:0] in_1,
  input  [15:0] in_2,
  output [15:0] out_3
);

  Multiplier #(.width(16)) multiplier_1 (.a(in_1), .b(in_2), .out(out_3));  // open: cin, cout
endmodule

module Divisor (
  input  [15:0] in_1,
  input  [15:0] in_2,
  output [15:0] out_3
);

  Divider #(.width(16)) divider_1 (.a(in_1), .b(in_2), .out(out_3));  // open: upper, rem
endmodule
