// Logisim project Genius.circ as structural Verilog: 2 circuits, main circuit Encoder
module Encoder (
  input  Reseta_a_memoria,
  input  in_2,
  output [1:0] out_3,
  output [1:0] Nova__cor,
  output [1:0] Cor__atual
);

  wire _0_out, _1_out, _2_out, _3_out, and_1_out, and_2_out, and_3_out, clock_1_out, comparador_1_out_2,
       comparador_1_out_3, comparador_1_out_4, comparador_1_out_5, comparator_1_gt, comparator_2_eq,
       counter_3_carry, not_1_out, not_2_out, not_3_out, not_4_out, or_1_out, or_2_out, or_3_out, or_4_out,
       or_5_out;
  wire [1:0] controlled_buffer_7_out, Random_out;
  wire [2:0] comparator_3_gt, register_1_q;
  wire [3:0] controlled_buffer_2_out, controlled_buffer_3_out, counter_1_q, counter_2_q, counter_3_q;

  Counter #(.width(4), .max('hf), .ongoal("stay"), .trigger("falling")) counter_1 (
    .Q(counter_1_q), .clk(and_1_out), .clr(or_2_out));  // open: load, D, count, carry
  and and_1 (and_1_out, and_3_out, not_1_out);
  or or_1 (or_1_out, or_4_out, and_1_out);
  Counter #(.width(4), .max('hf), .ongoal("stay"), .trigger("falling")) counter_2 (
    .Q(counter_2_q), .clk(and_2_out), .clr(or_1_out));  // open: load, D, count, carry
  or or_2 (or_2_out, comparator_2_eq, or_4_out);
  Comparator #(.width(4), .mode("unsigned")) comparator_1 (
    .a(counter_1_q), .b(counter_2_q), .gt(comparator_1_gt));  // open: eq, lt
  not not_1 (not_1_out, comparator_1_gt);
  and and_2 (and_2_out, and_3_out, comparator_1_gt);
  Comparator #(.width(4), .mode("unsigned")) comparator_2 (
    .a(counter_1_q), .b(4'b1111), .eq(comparator_2_eq));  // open: gt, lt
  Random #(.width(2)) Random (.clk(clock_1_out), .out(Random_out));  // open: next, clr
  assign Cor__atual = not_2_out ? Random_out : 2'bz;  // Controlled_Buffer controlled_buffer_1
  not not_2 (not_2_out, counter_3_carry);
  Counter #(.width(4), .max('hf), .ongoal("stay"), .trigger("falling")) counter_3 (
    .Q(counter_3_q), .carry(counter_3_carry), .clk(clock_1_out), .clr(Reseta_a_memoria));  // open: load, D, count
  assign controlled_buffer_2_out = not_2_out ? counter_3_q : 4'bz;  // Controlled_Buffer controlled_buffer_2
  assign controlled_buffer_3_out = not_2_out ? counter_3_q : 4'bz;  // Controlled_Buffer controlled_buffer_3
  assign controlled_buffer_2_out = counter_3_carry ? counter_1_q : 4'bz;  // Controlled_Buffer controlled_buffer_4
  assign Nova__cor = not_3_out ? Cor__atual : 2'bz;  // Controlled_Buffer controlled_buffer_5
  not not_3 (not_3_out, counter_3_carry);
  assign controlled_buffer_3_out = counter_3_carry ? counter_2_q : 4'bz;  // Controlled_Buffer controlled_buffer_6
  Button _3 (.out(_3_out));
  assign controlled_buffer_7_out = _3_out ? 2'b11 : 2'bz;  // Controlled_Buffer controlled_buffer_7
  Button _1 (.out(_1_out));
  Button _0 (.out(_0_out));
  Button _2 (.out(_2_out));
  assign controlled_buffer_7_out = _1_out ? 2'b01 : 2'bz;  // Controlled_Buffer controlled_buffer_8
  assign controlled_buffer_7_out = _2_out ? 2'b10 : 2'bz;  // Controlled_Buffer controlled_buffer_9
  assign controlled_buffer_7_out = _0_out ? 2'b00 : 2'bz;  // Controlled_Buffer controlled_buffer_10
  RAM #(.addrWidth(4), .dataWidth(2)) ram_1 (
    .addr(controlled_buffer_2_out), .data(Nova__cor), .clk(clock_1_out), .ld(counter_3_carry));  // open: sel, clr
  RAM #(.addrWidth(4), .dataWidth(2)) ram_2 (
    .addr(controlled_buffer_3_out), .data(Cor__atual), .clk(clock_1_out), .ld(counter_3_carry));  // open: sel, clr
  or or_3 (or_3_out, _3_out, _2_out, _1_out, _0_out);
  and and_3 (and_3_out, register_1_q[1], or_3_out);
  or or_4 (or_4_out, or_5_out, in_2);
  Comparador comparador_1 (
    .in_1(Nova__cor), .out_2(comparador_1_out_2), .out_3(comparador_1_out_3), .out_4(comparador_1_out_4),
    .out_5(comparador_1_out_5));
  Clock clock_1 (.out(clock_1_out));
  or or_5 (or_5_out, register_1_q[2], register_1_q[0]);
  LED led_1 (.in(comparador_1_out_2));
  LED led_2 (.in(comparador_1_out_4));
  LED led_3 (.in(comparador_1_out_5));
  LED led_4 (.in(comparador_1_out_3));
  Comparator #(.width(2), .mode("unsigned")) comparator_3 (
    .a(controlled_buffer_7_out), .b(Cor__atual), .gt(comparator_3_gt[0]), .eq(comparator_3_gt[1]),
    .lt(comparator_3_gt[2]));
  Register #(.width(3)) register_1 (
    .D(comparator_3_gt), .Q(register_1_q), .clk(clock_1_out), .clr(not_4_out));  // open: en
  not not_4 (not_4_out, or_3_out);

  // Notes on the sheet:
  //   Reseta os contadores
  //   LAÇO
  //   Memória
  //   Este é o numero
  //   a ser digitado agr
endmodule

module Comparador (
  input  [1:0] in_1,
  output out_2,
  output out_3,
  output out_4,
  output out_5
);

  wire not_1_out, not_2_out, not_3_out, not_4_out;

  not not_1 (not_1_out, in_1[0]);
  not not_2 (not_2_out, in_1[1]);
  not not_3 (not_3_out, in_1[1]);
  not not_4 (not_4_out, in_1[0]);
  and and_1 (out_2, not_1_out, not_2_out);
  and and_2 (out_3, in_1[0], not_3_out);
  and and_3 (out_4, not_4_out, in_1[1]);
  and and_4 (out_5, in_1[0], in_1[1]);
endmodule
