// Logisim project Main Calc Final.circ as structural Verilog: 18 circuits, main circuit main
module main (
  input  [15:0] in_1,
  input  [15:0] in_2,
  output [15:0] out_3
);

  wire and_2_out, and_3_out, and_4_out, and_out, \botões_1_out_5 , \botões_1_out_6 , button_2_out,
       button_3_out, button_4_out, button_out, circuito_display_1_s0, circuito_display_1_s1,
       circuito_display_1_s2, circuito_display_1_s3, circuito_display_1_s4, circuito_display_1_s5,
       circuito_display_1_s6, circuito_display_2_s0, circuito_display_2_s1, circuito_display_2_s2,
       circuito_display_2_s3, circuito_display_2_s4, circuito_display_2_s5, circuito_display_2_s6,
       circuito_display_3_s0, circuito_display_3_s1, circuito_display_3_s2, circuito_display_3_s3,
       circuito_display_3_s4, circuito_display_3_s5, circuito_display_3_s6, circuito_display_4_s0,
       circuito_display_4_s1, circuito_display_4_s2, circuito_display_4_s3, circuito_display_4_s4,
       circuito_display_4_s5, circuito_display_4_s6, circuito_display_5_s0, circuito_display_5_s1,
       circuito_display_5_s2, circuito_display_5_s3, circuito_display_5_s4, circuito_display_5_s5,
       circuito_display_5_s6, circuito_display_6_s0, circuito_display_6_s1, circuito_display_6_s2,
       circuito_display_6_s3, circuito_display_6_s4, circuito_display_6_s5, circuito_display_6_s6,
       circuito_display_7_s0, circuito_display_7_s1, circuito_display_7_s2, circuito_display_7_s3,
       circuito_display_7_s4, circuito_display_7_s5, circuito_display_7_s6, circuito_display_8_s0,
       circuito_display_8_s1, circuito_display_8_s2, circuito_display_8_s3, circuito_display_8_s4,
       circuito_display_8_s5, circuito_display_8_s6, circuito_display_9_s0, circuito_display_9_s1,
       circuito_display_9_s2, circuito_display_9_s3, circuito_display_9_s4, circuito_display_9_s5,
       circuito_display_9_s6, circuito_display_10_s0, circuito_display_10_s1, circuito_display_10_s2,
       circuito_display_10_s3, circuito_display_10_s4, circuito_display_10_s5, circuito_display_10_s6,
       circuito_display_11_s0, circuito_display_11_s1, circuito_display_11_s2, circuito_display_11_s3,
       circuito_display_11_s4, circuito_display_11_s5, circuito_display_11_s6, circuito_display_12_s0,
       circuito_display_12_s1, circuito_display_12_s2, circuito_display_12_s3, circuito_display_12_s4,
       circuito_display_12_s5, circuito_display_12_s6, not_1_out, not_2_out, not_3_out, not_4_out,
       operadores_display_1_l1, operadores_display_1_l2, operadores_display_1_l3, operadores_display_1_l4,
       operadores_display_1_l5, operadores_display_1_l6, operadores_display_1_l7, operadores_display_1_l8,
       operadores_display_1_l9;
  wire [3:0] separador_1_out_2, separador_1_out_3, separador_1_out_4, separador_1_out_5, separador_2_out_2,
       separador_2_out_3, separador_2_out_4, separador_2_out_5, separador_3_out_2, separador_3_out_3,
       separador_3_out_4, separador_3_out_5;
  wire [15:0] controlled_buffer_1_out, controlled_buffer_2_out, controlled_buffer_3_out,
       controlled_buffer_4_out, controlled_buffer_5_out, controlled_buffer_6_out, controlled_buffer_7_out,
       controlled_buffer_8_out, divisor_out_3, multiplicador_1_out_3, somador_16_bits_out_3,
       subtrator_16_bits_1_out_3;

  Circuito_Display circuito_display_1 (
    .a(separador_1_out_2[3]), .b(separador_1_out_2[2]), .c(separador_1_out_2[1]), .d(separador_1_out_2[0]),
    .s0(circuito_display_1_s0), .s1(circuito_display_1_s1), .s2(circuito_display_1_s2),
    .s3(circuito_display_1_s3), .s4(circuito_display_1_s4), .s5(circuito_display_1_s5),
    .s6(circuito_display_1_s6));
  Circuito_Display circuito_display_2 (
    .a(separador_2_out_2[3]), .b(separador_2_out_2[2]), .c(separador_2_out_2[1]), .d(separador_2_out_2[0]),
    .s0(circuito_display_2_s0), .s1(circuito_display_2_s1), .s2(circuito_display_2_s2),
    .s3(circuito_display_2_s3), .s4(circuito_display_2_s4), .s5(circuito_display_2_s5),
    .s6(circuito_display_2_s6));
  Circuito_Display circuito_display_3 (
    .a(separador_3_out_2[3]), .b(separador_3_out_2[2]), .c(separador_3_out_2[1]), .d(separador_3_out_2[0]),
    .s0(circuito_display_3_s0), .s1(circuito_display_3_s1), .s2(circuito_display_3_s2),
    .s3(circuito_display_3_s3), .s4(circuito_display_3_s4), .s5(circuito_display_3_s5),
    .s6(circuito_display_3_s6));
  not not_1 (not_1_out, \botões_1_out_5 );
  not not_2 (not_2_out, \botões_1_out_6 );
  and \and  (and_out, not_1_out, button_out, not_2_out);
  LED led_1 (.in(circuito_display_1_s6));
  LED led_2 (.in(circuito_display_1_s6));
  LED led_3 (.in(circuito_display_1_s4));
  LED led_4 (.in(circuito_display_1_s4));
  Separador separador_1 (
    .in_1(in_1), .out_2(separador_1_out_2), .out_3(separador_1_out_3), .out_4(separador_1_out_4),
    .out_5(separador_1_out_5));
  LED led_5 (.in(circuito_display_2_s6));
  LED led_6 (.in(circuito_display_2_s6));
  LED led_7 (.in(circuito_display_2_s4));
  LED led_8 (.in(circuito_display_2_s4));
  Separador separador_2 (
    .in_1(in_2), .out_2(separador_2_out_2), .out_3(separador_2_out_3), .out_4(separador_2_out_4),
    .out_5(separador_2_out_5));
  LED led_9 (.in(circuito_display_3_s6));
  LED led_10 (.in(circuito_display_3_s6));
  LED led_11 (.in(circuito_display_3_s4));
  LED led_12 (.in(circuito_display_3_s4));
  Separador separador_3 (
    .in_1(out_3), .out_2(separador_3_out_2), .out_3(separador_3_out_3), .out_4(separador_3_out_4),
    .out_5(separador_3_out_5));
  not not_3 (not_3_out, \botões_1_out_6 );
  not not_4 (not_4_out, \botões_1_out_5 );
  and and_2 (and_2_out, not_3_out, \botões_1_out_5 );
  LED led_13 (.in(circuito_display_1_s0));
  LED led_14 (.in(circuito_display_1_s0));
  LED led_15 (.in(circuito_display_1_s1));
  LED led_16 (.in(circuito_display_1_s1));
  LED led_17 (.in(circuito_display_1_s5));
  LED led_18 (.in(circuito_display_1_s5));
  LED led_19 (.in(circuito_display_1_s2));
  LED led_20 (.in(circuito_display_1_s2));
  LED led_21 (.in(circuito_display_1_s3));
  LED led_22 (.in(circuito_display_1_s3));
  LED led_23 (.in(circuito_display_2_s0));
  LED led_24 (.in(circuito_display_2_s0));
  LED led_25 (.in(circuito_display_2_s1));
  LED led_26 (.in(circuito_display_2_s1));
  LED led_27 (.in(circuito_display_2_s5));
  LED led_28 (.in(circuito_display_2_s5));
  LED led_29 (.in(circuito_display_2_s2));
  LED led_30 (.in(circuito_display_2_s2));
  LED led_31 (.in(circuito_display_2_s3));
  LED led_32 (.in(circuito_display_2_s3));
  LED led_33 (.in(circuito_display_3_s0));
  LED led_34 (.in(circuito_display_3_s0));
  LED led_35 (.in(circuito_display_3_s1));
  LED led_36 (.in(circuito_display_3_s1));
  LED led_37 (.in(circuito_display_3_s5));
  LED led_38 (.in(circuito_display_3_s5));
  LED led_39 (.in(circuito_display_3_s2));
  LED led_40 (.in(circuito_display_3_s2));
  LED led_41 (.in(circuito_display_3_s3));
  LED led_42 (.in(circuito_display_3_s3));
  and and_3 (and_3_out, \botões_1_out_6 , \botões_1_out_5 );
  and and_4 (and_4_out, not_4_out, \botões_1_out_6 );
  Circuito_Display circuito_display_4 (
    .a(separador_1_out_3[3]), .b(separador_1_out_3[2]), .c(separador_1_out_3[1]), .d(separador_1_out_3[0]),
    .s0(circuito_display_4_s0), .s1(circuito_display_4_s1), .s2(circuito_display_4_s2),
    .s3(circuito_display_4_s3), .s4(circuito_display_4_s4), .s5(circuito_display_4_s5),
    .s6(circuito_display_4_s6));
  Circuito_Display circuito_display_5 (
    .a(separador_2_out_3[3]), .b(separador_2_out_3[2]), .c(separador_2_out_3[1]), .d(separador_2_out_3[0]),
    .s0(circuito_display_5_s0), .s1(circuito_display_5_s1), .s2(circuito_display_5_s2),
    .s3(circuito_display_5_s3), .s4(circuito_display_5_s4), .s5(circuito_display_5_s5),
    .s6(circuito_display_5_s6));
  Circuito_Display circuito_display_6 (
    .a(separador_3_out_3[3]), .b(separador_3_out_3[2]), .c(separador_3_out_3[1]), .d(separador_3_out_3[0]),
    .s0(circuito_display_6_s0), .s1(circuito_display_6_s1), .s2(circuito_display_6_s2),
    .s3(circuito_display_6_s3), .s4(circuito_display_6_s4), .s5(circuito_display_6_s5),
    .s6(circuito_display_6_s6));
  assign controlled_buffer_1_out = and_out ? in_1 : 16'bz;  // Controlled_Buffer controlled_buffer_1
  Somador_16_Bits somador_16_bits (
    .in_1(controlled_buffer_1_out), .in_2(controlled_buffer_2_out), .out_3(somador_16_bits_out_3));
  assign controlled_buffer_2_out = and_out ? in_2 : 16'bz;  // Controlled_Buffer controlled_buffer_2
  assign controlled_buffer_3_out = and_2_out ? in_1 : 16'bz;  // Controlled_Buffer controlled_buffer_3
  assign controlled_buffer_4_out = and_2_out ? in_2 : 16'bz;  // Controlled_Buffer controlled_buffer_4
  Subtrator_16_Bits subtrator_16_bits_1 (
    .in_1(controlled_buffer_5_out), .in_2(controlled_buffer_6_out), .out_3(subtrator_16_bits_1_out_3));
  assign controlled_buffer_5_out = and_4_out ? in_1 : 16'bz;  // Controlled_Buffer controlled_buffer_5
  assign controlled_buffer_6_out = and_4_out ? in_2 : 16'bz;  // Controlled_Buffer controlled_buffer_6
  assign controlled_buffer_7_out = and_3_out ? in_1 : 16'bz;  // Controlled_Buffer controlled_buffer_7
  assign controlled_buffer_8_out = and_3_out ? in_2 : 16'bz;  // Controlled_Buffer controlled_buffer_8
  LED led_43 (.in(circuito_display_4_s6));
  LED led_44 (.in(circuito_display_4_s6));
  LED led_45 (.in(circuito_display_4_s4));
  LED led_46 (.in(circuito_display_4_s4));
  LED led_47 (.in(circuito_display_5_s6));
  LED led_48 (.in(circuito_display_5_s6));
  LED led_49 (.in(circuito_display_5_s4));
  LED led_50 (.in(circuito_display_5_s4));
  LED led_51 (.in(circuito_display_6_s6));
  LED led_52 (.in(circuito_display_6_s6));
  LED led_53 (.in(circuito_display_6_s4));
  LED led_54 (.in(circuito_display_6_s4));
  Button button (.out(button_out));
  Button button_2 (.out(button_2_out));
  Button button_3 (.out(button_3_out));
  Button button_4 (.out(button_4_out));
  assign out_3 = and_out ? somador_16_bits_out_3 : 16'bz;  // Controlled_Buffer controlled_buffer_9
  assign out_3 = and_2_out ? multiplicador_1_out_3 : 16'bz;  // Controlled_Buffer controlled_buffer_10
  Multiplicador multiplicador_1 (
    .in_1(controlled_buffer_3_out), .in_2(controlled_buffer_4_out), .out_3(multiplicador_1_out_3));
  assign out_3 = and_4_out ? subtrator_16_bits_1_out_3 : 16'bz;  // Controlled_Buffer controlled_buffer_11
  assign out_3 = and_3_out ? divisor_out_3 : 16'bz;  // Controlled_Buffer controlled_buffer_12
  Divisor divisor (.in_1(controlled_buffer_7_out), .in_2(controlled_buffer_8_out), .out_3(divisor_out_3));
  LED led_55 (.in(circuito_display_4_s0));
  LED led_56 (.in(circuito_display_4_s0));
  LED led_57 (.in(circuito_display_4_s5));
  LED led_58 (.in(circuito_display_4_s5));
  LED led_59 (.in(circuito_display_4_s3));
  LED led_60 (.in(circuito_display_4_s3));
  LED led_61 (.in(circuito_display_5_s0));
  LED led_62 (.in(circuito_display_5_s0));
  LED led_63 (.in(circuito_display_5_s5));
  LED led_64 (.in(circuito_display_5_s5));
  LED led_65 (.in(circuito_display_5_s3));
  LED led_66 (.in(circuito_display_5_s3));
  LED led_67 (.in(circuito_display_6_s0));
  LED led_68 (.in(circuito_display_6_s0));
  LED led_69 (.in(circuito_display_6_s5));
  LED led_70 (.in(circuito_display_6_s5));
  LED led_71 (.in(circuito_display_6_s3));
  LED led_72 (.in(circuito_display_6_s3));
  \Botões  \botões_1  (
    .b1(button_out), .b2(button_2_out), .out_5(\botões_1_out_5 ), .b3(button_3_out),
    .out_6(\botões_1_out_6 ), .b4(button_4_out));
  LED led_73 (.in(circuito_display_4_s1));
  LED led_74 (.in(circuito_display_4_s1));
  LED led_75 (.in(circuito_display_4_s2));
  LED led_76 (.in(circuito_display_4_s2));
  LED led_77 (.in(circuito_display_5_s1));
  LED led_78 (.in(circuito_display_5_s1));
  LED led_79 (.in(circuito_display_5_s2));
  LED led_80 (.in(circuito_display_5_s2));
  LED led_81 (.in(circuito_display_6_s1));
  LED led_82 (.in(circuito_display_6_s1));
  LED led_83 (.in(circuito_display_6_s2));
  LED led_84 (.in(circuito_display_6_s2));
  Circuito_Display circuito_display_7 (
    .a(separador_1_out_4[3]), .b(separador_1_out_4[2]), .c(separador_1_out_4[1]), .d(separador_1_out_4[0]),
    .s0(circuito_display_7_s0), .s1(circuito_display_7_s1), .s2(circuito_display_7_s2),
    .s3(circuito_display_7_s3), .s4(circuito_display_7_s4), .s5(circuito_display_7_s5),
    .s6(circuito_display_7_s6));
  Circuito_Display circuito_display_8 (
    .a(separador_2_out_4[3]), .b(separador_2_out_4[2]), .c(separador_2_out_4[1]), .d(separador_2_out_4[0]),
    .s0(circuito_display_8_s0), .s1(circuito_display_8_s1), .s2(circuito_display_8_s2),
    .s3(circuito_display_8_s3), .s4(circuito_display_8_s4), .s5(circuito_display_8_s5),
    .s6(circuito_display_8_s6));
  Circuito_Display circuito_display_9 (
    .a(separador_3_out_4[3]), .b(separador_3_out_4[2]), .c(separador_3_out_4[1]), .d(separador_3_out_4[0]),
    .s0(circuito_display_9_s0), .s1(circuito_display_9_s1), .s2(circuito_display_9_s2),
    .s3(circuito_display_9_s3), .s4(circuito_display_9_s4), .s5(circuito_display_9_s5),
    .s6(circuito_display_9_s6));
  LED led_85 (.in(circuito_display_7_s6));
  LED led_86 (.in(circuito_display_7_s6));
  LED led_87 (.in(circuito_display_7_s4));
  LED led_88 (.in(circuito_display_7_s4));
  LED led_89 (.in(circuito_display_8_s6));
  LED led_90 (.in(circuito_display_8_s6));
  LED led_91 (.in(circuito_display_8_s4));
  LED led_92 (.in(circuito_display_8_s4));
  LED led_93 (.in(circuito_display_9_s6));
  LED led_94 (.in(circuito_display_9_s6));
  LED led_95 (.in(circuito_display_9_s4));
  LED led_96 (.in(circuito_display_9_s4));
  LED led_97 (.in(circuito_display_7_s0));
  LED led_98 (.in(circuito_display_7_s0));
  LED led_99 (.in(circuito_display_7_s5));
  LED led_100 (.in(circuito_display_7_s5));
  LED led_101 (.in(circuito_display_7_s3));
  LED led_102 (.in(circuito_display_7_s3));
  LED led_103 (.in(circuito_display_8_s0));
  LED led_104 (.in(circuito_display_8_s0));
  LED led_105 (.in(circuito_display_8_s5));
  LED led_106 (.in(circuito_display_8_s5));
  LED led_107 (.in(circuito_display_8_s3));
  LED led_108 (.in(circuito_display_8_s3));
  LED led_109 (.in(circuito_display_9_s0));
  LED led_110 (.in(circuito_display_9_s0));
  LED led_111 (.in(circuito_display_9_s5));
  LED led_112 (.in(circuito_display_9_s5));
  LED led_113 (.in(circuito_display_9_s3));
  LED led_114 (.in(circuito_display_9_s3));
  LED led_115 (.in(circuito_display_7_s1));
  LED led_116 (.in(circuito_display_7_s1));
  LED led_117 (.in(circuito_display_7_s2));
  LED led_118 (.in(circuito_display_7_s2));
  LED led_119 (.in(circuito_display_8_s1));
  LED led_120 (.in(circuito_display_8_s1));
  LED led_121 (.in(circuito_display_8_s2));
  LED led_122 (.in(circuito_display_8_s2));
  LED led_123 (.in(circuito_display_9_s1));
  LED led_124 (.in(circuito_display_9_s1));
  LED led_125 (.in(circuito_display_9_s2));
  LED led_126 (.in(circuito_display_9_s2));
  Circuito_Display circuito_display_10 (
    .a(separador_1_out_5[3]), .b(separador_1_out_5[2]), .c(separador_1_out_5[1]), .d(separador_1_out_5[0]),
    .s0(circuito_display_10_s0), .s1(circuito_display_10_s1), .s2(circuito_display_10_s2),
    .s3(circuito_display_10_s3), .s4(circuito_display_10_s4), .s5(circuito_display_10_s5),
    .s6(circuito_display_10_s6));
  Circuito_Display circuito_display_11 (
    .a(separador_2_out_5[3]), .b(separador_2_out_5[2]), .c(separador_2_out_5[1]), .d(separador_2_out_5[0]),
    .s0(circuito_display_11_s0), .s1(circuito_display_11_s1), .s2(circuito_display_11_s2),
    .s3(circuito_display_11_s3), .s4(circuito_display_11_s4), .s5(circuito_display_11_s5),
    .s6(circuito_display_11_s6));
  Circuito_Display circuito_display_12 (
    .a(separador_3_out_5[3]), .b(separador_3_out_5[2]), .c(separador_3_out_5[1]), .d(separador_3_out_5[0]),
    .s0(circuito_display_12_s0), .s1(circuito_display_12_s1), .s2(circuito_display_12_s2),
    .s3(circuito_display_12_s3), .s4(circuito_display_12_s4), .s5(circuito_display_12_s5),
    .s6(circuito_display_12_s6));
  LED led_127 (.in(circuito_display_10_s0));
  LED led_128 (.in(circuito_display_10_s0));
  LED led_129 (.in(circuito_display_10_s6));
  LED led_130 (.in(circuito_display_10_s6));
  LED led_131 (.in(circuito_display_10_s5));
  LED led_132 (.in(circuito_display_10_s5));
  LED led_133 (.in(circuito_display_10_s4));
  LED led_134 (.in(circuito_display_10_s4));
  LED led_135 (.in(circuito_display_10_s3));
  LED led_136 (.in(circuito_display_10_s3));
  LED led_137 (.in(circuito_display_11_s0));
  LED led_138 (.in(circuito_display_11_s0));
  LED led_139 (.in(circuito_display_11_s6));
  LED led_140 (.in(circuito_display_11_s6));
  LED led_141 (.in(circuito_display_11_s5));
  LED led_142 (.in(circuito_display_11_s5));
  LED led_143 (.in(circuito_display_11_s4));
  LED led_144 (.in(circuito_display_11_s4));
  LED led_145 (.in(circuito_display_11_s3));
  LED led_146 (.in(circuito_display_11_s3));
  LED led_147 (.in(circuito_display_12_s0));
  LED led_148 (.in(circuito_display_12_s0));
  LED led_149 (.in(circuito_display_12_s6));
  LED led_150 (.in(circuito_display_12_s6));
  LED led_151 (.in(circuito_display_12_s5));
  LED led_152 (.in(circuito_display_12_s5));
  LED led_153 (.in(circuito_display_12_s4));
  LED led_154 (.in(circuito_display_12_s4));
  LED led_155 (.in(circuito_display_12_s3));
  LED led_156 (.in(circuito_display_12_s3));
  LED led_157 (.in(circuito_display_10_s1));
  LED led_158 (.in(circuito_display_10_s1));
  LED led_159 (.in(circuito_display_10_s2));
  LED led_160 (.in(circuito_display_10_s2));
  LED led_161 (.in(circuito_display_11_s1));
  LED led_162 (.in(circuito_display_11_s1));
  LED led_163 (.in(circuito_display_11_s2));
  LED led_164 (.in(circuito_display_11_s2));
  LED led_165 (.in(circuito_display_12_s1));
  LED led_166 (.in(circuito_display_12_s1));
  LED led_167 (.in(circuito_display_12_s2));
  LED led_168 (.in(circuito_display_12_s2));
  LED led_169 (.in(operadores_display_1_l2));
  LED led_170 (.in(operadores_display_1_l1));
  LED led_171 (.in(operadores_display_1_l4));
  LED led_172 (.in(operadores_display_1_l5));
  LED led_173 (.in(operadores_display_1_l7));
  LED led_174 (.in(operadores_display_1_l8));
  LED led_175 (.in(1'b1));
  LED led_176 (.in(1'b1));
  LED led_177 ();  // open: in
  LED led_178 ();  // open: in
  LED led_179 (.in(1'b1));
  LED led_180 (.in(1'b1));
  Operadores_Display operadores_display_1 (
    .a(button_out), .b(button_2_out), .c(button_3_out), .d(button_4_out), .L1(operadores_display_1_l1),
    .L2(operadores_display_1_l2), .L3(operadores_display_1_l3), .L4(operadores_display_1_l4),
    .L5(operadores_display_1_l5), .L6(operadores_display_1_l6), .L7(operadores_display_1_l7),
    .L8(operadores_display_1_l8), .L9(operadores_display_1_l9));
  LED led_181 (.in(operadores_display_1_l3));
  LED led_182 (.in(operadores_display_1_l6));
  LED led_183 (.in(operadores_display_1_l9));
  LED led_184 (.in(1'b1));
  LED led_185 ();  // open: in
  LED led_186 (.in(1'b1));

  // Notes on the sheet:
  //   Output
  //   Input 2 (Inferior)
  //   Input 1 (Superior)
  //   Input 2 (Superior)
  //   Input 1 (Superior)
  //   Sinal de Igual
  //   Operações + - * /
endmodule

module Multiplicador_2_Bits (
  input  in_1,
  input  in_2,
  input  in_3,
  input  in_4,
  output out_5,
  output out_6,
  output out_7,
  output out_8
);

  wire and_1_out, and_3_out, and_4_out, and_5_out;

  and and_1 (and_1_out, in_1, in_4);
  and and_2 (out_5, in_1, in_3);
  and and_3 (and_3_out, in_2, in_3);
  and and_4 (and_4_out, in_2, in_4);
  xor xor_1 (out_6, and_1_out, and_3_out);
  and and_5 (and_5_out, and_1_out, and_3_out);
  xor xor_2 (out_7, and_5_out, and_4_out);
  and and_6 (out_8, and_5_out, and_4_out);
endmodule

module MSomador (
  input  A,
  input  B,
  output out_3,
  output out_4
);

  and and_1 (out_3, A, B);
  xor xor_1 (out_4, A, B);
endmodule

module MSubtrator (
  input  A,
  input  B,
  output out_3,
  output out_4
);

  wire not_1_out;

  not not_1 (not_1_out, A);
  and and_1 (out_4, B, not_1_out);
  xor xor_1 (out_3, A, B);
endmodule

module SomadorC (
  input  A,
  input  B,
  input  C,
  output out_4,
  output out_5
);

  wire and_1_out, and_2_out, xor_1_out, xor_2_out;

  xor xor_1 (xor_1_out, A, B);
  xor xor_2 (xor_2_out, B, C);
  xor xor_3 (out_4, xor_1_out, C);
  and and_1 (and_1_out, C, B);
  and and_2 (and_2_out, A, xor_2_out);
  or or_1 (out_5, and_1_out, and_2_out);
endmodule

module SubtratorC (
  input  A,
  input  B,
  input  C,
  output out_4,
  output out_5
);

  wire and_1_out, and_2_out, not_1_out, not_2_out, xor_1_out;

  not not_1 (not_1_out, xor_1_out);
  xor xor_1 (xor_1_out, A, B);
  and and_1 (and_1_out, not_1_out, C);
  not not_2 (not_2_out, A);
  xor xor_2 (out_4, xor_1_out, C);
  and and_2 (and_2_out, not_2_out, B);
  or or_1 (out_5, and_1_out, and_2_out);
endmodule

module Somador_16_Bits (
  input  [15:0] in_1,
  input  [15:0] in_2,
  output [15:0] out_3
);

  wire msomador_1_out_3, somadorc_1_out_5, somadorc_3_out_5, somadorc_4_out_5, somadorc_5_out_5,
       somadorc_6_out_5, somadorc_7_out_5, somadorc_8_out_5, somadorc_9_out_5, somadorc_10_out_5,
       somadorc_11_out_5, somadorc_12_out_5, somadorc_13_out_5, somadorc_14_out_5, somadorc_15_out_5;

  SomadorC somadorc_1 (.A(somadorc_3_out_5), .B(in_1[14]), .C(in_2[14]), .out_4(out_3[14]), .out_5(somadorc_1_out_5));
  SomadorC somadorc_2 (.A(somadorc_1_out_5), .B(in_1[15]), .C(in_2[15]), .out_4(out_3[15]));  // open: out_5
  SomadorC somadorc_3 (.A(somadorc_4_out_5), .B(in_1[13]), .C(in_2[13]), .out_4(out_3[13]), .out_5(somadorc_3_out_5));
  SomadorC somadorc_4 (.A(somadorc_6_out_5), .B(in_1[12]), .C(in_2[12]), .out_4(out_3[12]), .out_5(somadorc_4_out_5));
  SomadorC somadorc_5 (.A(somadorc_8_out_5), .B(in_1[10]), .C(in_2[10]), .out_4(out_3[10]), .out_5(somadorc_5_out_5));
  SomadorC somadorc_6 (.A(somadorc_5_out_5), .B(in_1[11]), .C(in_2[11]), .out_4(out_3[11]), .out_5(somadorc_6_out_5));
  SomadorC somadorc_7 (.A(somadorc_9_out_5), .B(in_1[8]), .C(in_2[8]), .out_4(out_3[8]), .out_5(somadorc_7_out_5));
  SomadorC somadorc_8 (.A(somadorc_7_out_5), .B(in_1[9]), .C(in_2[9]), .out_4(out_3[9]), .out_5(somadorc_8_out_5));
  SomadorC somadorc_9 (.A(somadorc_10_out_5), .B(in_1[7]), .C(in_2[7]), .out_4(out_3[7]), .out_5(somadorc_9_out_5));
  SomadorC somadorc_10 (.A(somadorc_11_out_5), .B(in_1[6]), .C(in_2[6]), .out_4(out_3[6]), .out_5(somadorc_10_out_5));
  SomadorC somadorc_11 (.A(somadorc_12_out_5), .B(in_1[5]), .C(in_2[5]), .out_4(out_3[5]), .out_5(somadorc_11_out_5));
  SomadorC somadorc_12 (.A(somadorc_14_out_5), .B(in_1[4]), .C(in_2[4]), .out_4(out_3[4]), .out_5(somadorc_12_out_5));
  SomadorC somadorc_13 (.A(somadorc_15_out_5), .B(in_1[2]), .C(in_2[2]), .out_4(out_3[2]), .out_5(somadorc_13_out_5));
  SomadorC somadorc_14 (.A(somadorc_13_out_5), .B(in_1[3]), .C(in_2[3]), .out_4(out_3[3]), .out_5(somadorc_14_out_5));
  SomadorC somadorc_15 (.A(msomador_1_out_3), .B(in_1[1]), .C(in_2[1]), .out_4(out_3[1]), .out_5(somadorc_15_out_5));
  MSomador msomador_1 (.A(in_1[0]), .B(in_2[0]), .out_3(msomador_1_out_3), .out_4(out_3[0]));
endmodule

module Subtrator_16_Bits (
  input  [15:0] in_1,
  input  [15:0] in_2,
  output [15:0] out_3
);

  wire msubtrator_1_out_4, subtratorc_2_out_5, subtratorc_3_out_5, subtratorc_4_out_5, subtratorc_5_out_5,
       subtratorc_6_out_5, subtratorc_7_out_5, subtratorc_8_out_5, subtratorc_9_out_5, subtratorc_10_out_5,
       subtratorc_11_out_5, subtratorc_12_out_5, subtratorc_13_out_5, subtratorc_14_out_5,
       subtratorc_15_out_5;

  SubtratorC subtratorc_1 (.A(in_1[15]), .B(subtratorc_2_out_5), .C(in_2[15]), .out_4(out_3[15]));  // open: out_5
  SubtratorC subtratorc_2 (
    .A(in_1[14]), .B(subtratorc_3_out_5), .C(in_2[14]), .out_4(out_3[14]), .out_5(subtratorc_2_out_5));
  SubtratorC subtratorc_3 (
    .A(in_1[13]), .B(subtratorc_4_out_5), .C(in_2[13]), .out_4(out_3[13]), .out_5(subtratorc_3_out_5));
  SubtratorC subtratorc_4 (
    .A(in_1[12]), .B(subtratorc_6_out_5), .C(in_2[12]), .out_4(out_3[12]), .out_5(subtratorc_4_out_5));
  SubtratorC subtratorc_5 (
    .A(in_1[10]), .B(subtratorc_7_out_5), .C(in_2[10]), .out_4(out_3[10]), .out_5(subtratorc_5_out_5));
  SubtratorC subtratorc_6 (
    .A(in_1[11]), .B(subtratorc_5_out_5), .C(in_2[11]), .out_4(out_3[11]), .out_5(subtratorc_6_out_5));
  SubtratorC subtratorc_7 (
    .A(in_1[9]), .B(subtratorc_8_out_5), .C(in_2[9]), .out_4(out_3[9]), .out_5(subtratorc_7_out_5));
  SubtratorC subtratorc_8 (
    .A(in_1[8]), .B(subtratorc_10_out_5), .C(in_2[8]), .out_4(out_3[8]), .out_5(subtratorc_8_out_5));
  SubtratorC subtratorc_9 (
    .A(in_1[6]), .B(subtratorc_11_out_5), .C(in_2[6]), .out_4(out_3[6]), .out_5(subtratorc_9_out_5));
  SubtratorC subtratorc_10 (
    .A(in_1[7]), .B(subtratorc_9_out_5), .C(in_2[7]), .out_4(out_3[7]), .out_5(subtratorc_10_out_5));
  SubtratorC subtratorc_11 (
    .A(in_1[5]), .B(subtratorc_12_out_5), .C(in_2[5]), .out_4(out_3[5]), .out_5(subtratorc_11_out_5));
  SubtratorC subtratorc_12 (
    .A(in_1[4]), .B(subtratorc_14_out_5), .C(in_2[4]), .out_4(out_3[4]), .out_5(subtratorc_12_out_5));
  SubtratorC subtratorc_13 (
    .A(in_1[2]), .B(subtratorc_15_out_5), .C(in_2[2]), .out_4(out_3[2]), .out_5(subtratorc_13_out_5));
  SubtratorC subtratorc_14 (
    .A(in_1[3]), .B(subtratorc_13_out_5), .C(in_2[3]), .out_4(out_3[3]), .out_5(subtratorc_14_out_5));
  MSubtrator msubtrator_1 (.A(in_1[0]), .B(in_2[0]), .out_4(msubtrator_1_out_4), .out_3(out_3[0]));
  SubtratorC subtratorc_15 (
    .A(in_1[1]), .B(msubtrator_1_out_4), .C(in_2[1]), .out_4(out_3[1]), .out_5(subtratorc_15_out_5));
endmodule

module Inversor (
  input  [15:0] in_1,
  output [15:0] out_2
);

  not not_1 (out_2[0], in_1[0]);
  not not_2 (out_2[1], in_1[1]);
  not not_3 (out_2[2], in_1[2]);
  not not_4 (out_2[3], in_1[3]);
  not not_5 (out_2[4], in_1[4]);
  not not_6 (out_2[5], in_1[5]);
  not not_7 (out_2[6], in_1[6]);
  not not_8 (out_2[7], in_1[7]);
  not not_9 (out_2[8], in_1[8]);
  not not_10 (out_2[9], in_1[9]);
  not not_11 (out_2[10], in_1[10]);
  not not_12 (out_2[11], in_1[11]);
  not not_13 (out_2[12], in_1[12]);
  not not_14 (out_2[13], in_1[13]);
  not not_15 (out_2[14], in_1[14]);
  not not_16 (out_2[15], in_1[15]);
endmodule

module \Botões  (
  input  b1,
  input  b2,
  input  b3,
  input  b4,
  output out_5,
  output out_6
);

  wire and_1_out, and_2_out, not_1_out, not_2_out;

  not not_1 (not_1_out, b1);
  not not_2 (not_2_out, b4);
  and and_1 (and_1_out, not_1_out, b3);
  and and_2 (and_2_out, b2, not_2_out);
  or or_1 (out_5, and_1_out, b4);
  or or_2 (out_6, and_2_out, b4);
endmodule

// *
module Multiplicador (
  input  [15:0] in_1,
  input  [15:0] in_2,
  output [15:0] out_3
);

  Multiplier #(.width(16)) multiplier_1 (.a(in_1), .b(in_2), .out(out_3));  // open: cin, cout
endmodule

module Divisor (
  input  [15:0] in_1,
  input  [15:0] in_2,
  output [15:0] out_3
);

  Divider #(.width(16)) divider_1 (.a(in_1), .b(in_2), .out(out_3));  // open: upper, rem
endmodule

module Subtrator (
  input  [15:0] in_1,
  input  [15:0] in_2,
  output [15:0] out_3
);

  Subtractor #(.width(16)) subtractor_1 (.a(in_1), .b(in_2), .out(out_3));  // open: bin, bout
endmodule

module Igual_Display (
  input  a,
  output L1,
  output L2,
  output L3,
  output L4,
  output L5,
  output L6,
  output L7,
  output L8,
  output L9
);


  assign L1 = 1'b1;
  assign L2 = 1'b1;
  assign L3 = 1'b1;
  assign L4 = 1'b1;
  assign L5 = 1'b1;
  assign L6 = 1'b1;
  assign L7 = 1'b1;
  assign L8 = 1'b1;
  assign L9 = 1'b1;
endmodule

module Operadores_Display (
  input  a,
  input  b,
  input  c,
  input  d,
  output L1,
  output L2,
  output L3,
  output L4,
  output L5,
  output L6,
  output L7,
  output L8,
  output L9
);

  wire and_1_out, and_2_out, and_3_out, and_4_out, and_5_out, and_6_out, and_7_out, and_8_out, and_9_out,
       and_10_out, not_1_out, not_2_out;

  and and_1 (and_1_out, b, d);
  and and_2 (and_2_out, a, b);
  and and_3 (and_3_out, b, d);
  and and_4 (and_4_out, a, b);
  and and_5 (and_5_out, b, not_1_out);
  not not_1 (not_1_out, d);
  or or_1 (L5, d, c, b, a);
  and and_6 (and_6_out, b, not_2_out);
  not not_2 (not_2_out, d);
  and and_7 (and_7_out, a, b);
  and and_8 (and_8_out, b, d);
  and and_9 (and_9_out, b, d);
  and and_10 (and_10_out, a, b);
  or or_2 (L1, c, and_1_out, and_2_out);
  or or_3 (L2, c, and_3_out, a);
  or or_4 (L3, d, c, and_4_out);
  or or_5 (L4, c, and_5_out, a);
  or or_6 (L6, c, and_6_out, a);
  or or_7 (L7, d, c, and_7_out);
  or or_8 (L8, c, and_8_out, a);
  or or_9 (L9, c, and_9_out, and_10_out);
endmodule

module Circuito_Display (
  input  a,
  input  b,
  input  c,
  input  d,
  output s0,
  output s1,
  output s2,
  output s3,
  output s4,
  output s5,
  output s6
);

  wire and_1_out, and_2_out, and_3_out, and_4_out, and_5_out, and_6_out, and_7_out, and_8_out, and_9_out,
       and_10_out, and_11_out, and_12_out, and_13_out, and_14_out, and_15_out, and_16_out, and_17_out,
       and_18_out, and_19_out, and_20_out, and_21_out, and_22_out, and_23_out, and_24_out, and_25_out,
       and_26_out, and_27_out, and_28_out, and_29_out, not_1_out, not_2_out, not_3_out, not_4_out, not_5_out,
       not_6_out, not_7_out, not_8_out, not_9_out, not_10_out, not_11_out, not_12_out, not_13_out,
       not_14_out, not_15_out, not_16_out, not_17_out, not_18_out, not_19_out, not_20_out, not_21_out,
       not_22_out, not_23_out, not_24_out, not_25_out, not_26_out, not_27_out, not_28_out, not_29_out,
       not_30_out, not_31_out, not_32_out, not_33_out, not_34_out, not_35_out, not_36_out, not_37_out,
       not_38_out, not_39_out, not_40_out, not_41_out, not_42_out, not_43_out, not_44_out, not_45_out,
       not_46_out;

  not not_1 (not_1_out, a);
  and and_1 (and_1_out, not_1_out, not_2_out, not_3_out);
  not not_2 (not_2_out, b);
  not not_3 (not_3_out, d);
  not not_4 (not_4_out, a);
  and and_2 (and_2_out, not_4_out, c);
  not not_5 (not_5_out, a);
  and and_3 (and_3_out, not_5_out, b, d);
  and and_4 (and_4_out, b, c, d);
  not not_6 (not_6_out, b);
  and and_5 (and_5_out, a, not_6_out, not_7_out);
  not not_7 (not_7_out, c);
  not not_8 (not_8_out, a);
  and and_6 (and_6_out, not_8_out, not_9_out);
  not not_9 (not_9_out, b);
  not not_10 (not_10_out, a);
  and and_7 (and_7_out, not_10_out, not_11_out, not_12_out);
  not not_11 (not_11_out, c);
  not not_12 (not_12_out, d);
  not not_13 (not_13_out, b);
  and and_8 (and_8_out, not_13_out, not_14_out);
  not not_14 (not_14_out, c);
  and and_9 (and_9_out, b, c, d);
  not not_15 (not_15_out, b);
  and and_10 (and_10_out, not_15_out, not_16_out);
  not not_16 (not_16_out, c);
  not not_17 (not_17_out, a);
  and and_11 (and_11_out, not_17_out, d);
  not not_18 (not_18_out, a);
  and and_12 (and_12_out, not_18_out, b);
  and and_13 (and_13_out, b, c, d);
  not not_19 (not_19_out, b);
  not not_20 (not_20_out, c);
  not not_21 (not_21_out, d);
  not not_22 (not_22_out, a);
  not not_23 (not_23_out, b);
  not not_24 (not_24_out, a);
  not not_25 (not_25_out, d);
  not not_26 (not_26_out, a);
  not not_27 (not_27_out, c);
  not not_28 (not_28_out, b);
  and and_14 (and_14_out, not_28_out, not_29_out, not_30_out);
  not not_29 (not_29_out, c);
  not not_30 (not_30_out, d);
  not not_31 (not_31_out, a);
  and and_15 (and_15_out, not_31_out, c, not_32_out);
  not not_32 (not_32_out, d);
  and and_16 (and_16_out, a, b, c, d);
  not not_33 (not_33_out, a);
  not not_34 (not_34_out, b);
  and and_17 (and_17_out, not_33_out, not_34_out, c);
  not not_35 (not_35_out, a);
  and and_18 (and_18_out, not_35_out, b, not_36_out);
  not not_36 (not_36_out, c);
  not not_37 (not_37_out, a);
  and and_19 (and_19_out, not_37_out, b, not_38_out);
  not not_38 (not_38_out, d);
  and and_20 (and_20_out, a, not_39_out, not_40_out);
  not not_39 (not_39_out, b);
  not not_40 (not_40_out, c);
  not not_41 (not_41_out, a);
  and and_21 (and_21_out, not_41_out, not_42_out, not_43_out);
  not not_42 (not_42_out, c);
  not not_43 (not_43_out, d);
  not not_44 (not_44_out, a);
  and and_22 (and_22_out, not_44_out, b);
  and and_23 (and_23_out, b, c, d);
  and and_24 (and_24_out, a, not_45_out, not_46_out);
  not not_45 (not_45_out, b);
  not not_46 (not_46_out, c);
  or or_1 (s0, and_1_out, and_2_out, and_3_out, and_4_out, and_5_out);
  or or_2 (s1, and_6_out, and_7_out, and_8_out, and_9_out);
  or or_3 (s2, and_10_out, and_11_out, and_12_out, and_13_out);
  and and_25 (and_25_out, not_19_out, not_20_out, not_21_out);
  and and_26 (and_26_out, not_22_out, not_23_out, c);
  and and_27 (and_27_out, not_24_out, c, not_25_out);
  and and_28 (and_28_out, not_26_out, b, not_27_out, d);
  and and_29 (and_29_out, a, b, c, d);
  or or_4 (s4, and_14_out, and_15_out, and_16_out);
  or or_5 (s5, and_17_out, and_18_out, and_19_out, and_20_out);
  or or_6 (s6, and_21_out, and_22_out, and_23_out, and_24_out);
  or or_7 (s3, and_25_out, and_26_out, and_27_out, and_28_out, and_29_out);
endmodule

module Display (
  input  [3:0] in_1
);

  wire circuito_display_1_s0, circuito_display_1_s1, circuito_display_1_s2, circuito_display_1_s3,
       circuito_display_1_s4, circuito_display_1_s5, circuito_display_1_s6;

  Circuito_Display circuito_display_1 (
    .a(in_1[3]), .b(in_1[2]), .c(in_1[1]), .d(in_1[0]), .s0(circuito_display_1_s0),
    .s1(circuito_display_1_s1), .s2(circuito_display_1_s2), .s3(circuito_display_1_s3),
    .s4(circuito_display_1_s4), .s5(circuito_display_1_s5), .s6(circuito_display_1_s6));
  LED led_1 (.in(circuito_display_1_s6));
  LED led_2 (.in(circuito_display_1_s6));
  LED led_3 (.in(circuito_display_1_s4));
  LED led_4 (.in(circuito_display_1_s4));
  LED led_5 (.in(circuito_display_1_s0));
  LED led_6 (.in(circuito_display_1_s0));
  LED led_7 (.in(circuito_display_1_s5));
  LED led_8 (.in(circuito_display_1_s5));
  LED led_9 (.in(circuito_display_1_s3));
  LED led_10 (.in(circuito_display_1_s3));
  LED led_11 (.in(circuito_display_1_s1));
  LED led_12 (.in(circuito_display_1_s1));
  LED led_13 (.in(circuito_display_1_s2));
  LED led_14 (.in(circuito_display_1_s2));
endmodule

module Separador (
  input  [15:0] in_1,
  output [3:0] out_2,
  output [3:0] out_3,
  output [3:0] out_4,
  output [3:0] out_5
);

  wire [15:0] multiplier_1_out, multiplier_2_out, multiplier_3_out, subtractor_1_out, subtractor_2_out;
  wire [15:4] divider_1_out, divider_2_out, divider_3_out, subtractor_3_out;

  Divider #(.width(16)) divider_1 (.a(in_1), .b(16'h3e8), .out({divider_1_out, out_2}));  // open: upper, rem
  Multiplier #(.width(16)) multiplier_1 (
    .a(16'h3e8), .b({divider_1_out, out_2}), .out(multiplier_1_out));  // open: cin, cout
  Subtractor #(.width(16)) subtractor_1 (.a(in_1), .b(multiplier_1_out), .out(subtractor_1_out));  // open: bin, bout
  Divider #(.width(16)) divider_2 (.a(subtractor_1_out), .b(16'h64), .out({divider_2_out, out_3}));  // open: upper, rem
  Multiplier #(.width(16)) multiplier_2 (
    .a(16'h64), .b({divider_2_out, out_3}), .out(multiplier_2_out));  // open: cin, cout
  Subtractor #(.width(16)) subtractor_2 (
    .a(subtractor_1_out), .b(multiplier_2_out), .out(subtractor_2_out));  // open: bin, bout
  Divider #(.width(16)) divider_3 (.a(subtractor_2_out), .b(16'ha), .out({divider_3_out, out_4}));  // open: upper, rem
  Multiplier #(.width(16)) multiplier_3 (
    .a(16'ha), .b({divider_3_out, out_4}), .out(multiplier_3_out));  // open: cin, cout
  Subtractor #(.width(16)) subtractor_3 (
    .a(subtractor_2_out), .b(multiplier_3_out), .out({subtractor_3_out, out_5}));  // open: bin, bout
endmodule
